# Fritzing sketch Esquematico (saved by Fritzing 0.9.4)
breadboards: 1

parts:
  M1 = ESP-01 Breakout Board Breadboard Adapter [part_number=ESP8266]
  L298N1 = L298N DC motor driver
  Componente2 = Arduino Uno (Rev3)
  U2 = SWITCH-SPST-2 [package=switch-spst-vertical]
  VCC1 = Battery block 9V
  VCC2 = 4 x AAA Battery Mount
  M2 = DC Motor
  M3 = DC Motor
  R1 = Resistor [tolerance=±5% resistance=1k package=THT]
  R2 = Resistor [tolerance=±5% resistance=22k package=THT]
  U4 = SWITCH-SPST-2 [package=switch-spst-vertical]
  Q1 = NPN-Transistor [package="TO92 [THT]"]
  U5 = Mini-360 DC-DC Buck converter [package=THT]

nets:
  N1: M1.TXD, Componente2.D0/RX
  N2: M1.CHPD, M1.RST, M1.VCC, R2.Pin_1, U5.OUT+
  N3: M1.GP0, Componente2.D4
  N4: M1.GP2, R2.Pin_0, Q1.E
  N5: M1.GND, Q1.C, U5.OUT-
  N6: L298N1.OUT1, M2.pin_2
  N7: L298N1.OUT2, M2.pin_1
  N8: L298N1.OUT3, M3.pin_2
  N9: L298N1.OUT4, M3.pin_1
  N10: L298N1.12V, U4.P
  GND: L298N1.GND, Componente2.GND, VCC1.-, VCC2.-, U5.IN-
  N11: L298N1.5V#9, L298N1.ENA
  N12: L298N1.5V#10, L298N1.ENB
  N13: L298N1.IN1, Componente2.D3_PWM
  N14: L298N1.IN2, Componente2.D5_PWM
  N15: L298N1.IN3, Componente2.D9_PWM
  N16: L298N1.IN4, Componente2.D10_PWM/SS
  N17: Componente2.D2, R1.Pin_1
  N18: Componente2.VIN, U2.O, U5.IN+
  N19: U2.P, VCC1.+
  N20: VCC2.+, U4.O
  N21: R1.Pin_0, Q1.B

custom parts:
  ESP-01 Breakout Board Breadboard Adapter: Generic WiFi Module based on the ESP8266 with onboard PCB antenna and UART communications with breadboard friendly breakout board attached.
  L298N DC motor driver: 2x DC motor driver with 78M05 positive voltage regulator (7..35 V) L298N: max 46 V, 2 A Set 5 V Enable jumper to enable 5 V regultor (needed for the L298N) and +5 V output at screw terminal or supply external +5 V at screw terminal Set ENA and/or ENB to +5 V to enable motor permanently or supply ENA and/or ENB with PWM signal IN1 and IN2 set rotation directory for motor A (OUT1/OUT2) IN2 and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
  Mini-360 DC-DC Buck converter: Mini-360 DC-DC Buck converter. Tiny buck step down voltage converter, input voltage 4.75 to 23V output 1 to 17V adjustable. Available from ebay and the like.
